// Logisim project DDCA sem1.circ as structural Verilog: 1 circuit, main circuit main
module main (
  input  in_1,
  input  in_2,
  input  in_3,
  input  in_4,
  input  a,
  input  b,
  input  a_2,
  input  b_2,
  input  c,
  input  in_10,
  output out_11,
  output out_12,
  output carry,
  output sum
);

  wire and_2_out, and_3_out, and_4_out, xor_2_out;

  and and_1 (out_11, in_1, in_3);
  and and_2 (and_2_out, a, b);
  and and_3 (and_3_out, b, c);
  and and_4 (and_4_out, c, a);
  or or_1 (carry, and_2_out, and_3_out, and_4_out);
  xor xor_1 (out_12, in_2, in_4);
  xor xor_2 (xor_2_out, a_2, b_2);
  xor xor_3 (sum, xor_2_out, in_10);
endmodule
